# Fritzing sketch flusher (saved by Fritzing 0.8.0b)
breadboards: 1

parts:
  Part1 = Arduino Uno (Rev3)
  J1 = PING))) Ultrasonic Distance Sensor [package="3-pin SIP, 0.1\" spacing(ground,power,signal)"]
  J2 = Basic Servo
  LED1 = smd LED [color="Red (633nm)" package="1206 [SMD]"]
  S1 = Pushbutton [package="[SMD]"]
  R2 = Resistor [tolerance=±5% resistance=220 package="1206 [SMD]"]
  R1 = Resistor [tolerance=±5% resistance=10k package="1206 [SMD]"]

nets:
  GND: Part1.GND, J1.GND(vss), J2.gnd, LED1.cathode, S1.Pin_1, S1.Pin_2
  N1: Part1.D9_PWM, J2.pulse
  N2: Part1.D10_PWM/SS, S1.Pin_3, S1.Pin_4, R1.Pin_1
  N3: Part1.D11_PWM/MOSI, J1.SIG
  N4: Part1.D12/MISO, R2.Pin_1
  5V: Part1.5V, J1.5_V(vdd), J2.vcc, R1.Pin_0
  N5: LED1.anode, R2.Pin_0

notes:
  Fritzing does not have the proper sensor,
  this is it's closest match.
  (wires on sensor aren't color-coded properly)
  Same as on the breadboad...
  Flusher

custom parts:
  PING))) Ultrasonic Distance Sensor: The Parallax PING))) ultrasonic distance sensor provides precise, non-contact distance measurements from about 2 cm (0.8 inches) to 3 meters (3.3 yards). It is very easy to connect to BASIC Stamp® or Javelin Stamp microcontrollers, requiring only one I/O pin.
