# Fritzing sketch SimpleSimon_updatedFritzing (saved by Fritzing 0.9.3b)
circuit board: 10.1776cm x 5.36194cm
breadboards: 1

parts:
  LED1 = LED - 5mm [color="Green (565nm)" package="5 mm [THT]"]
  SPKR1 = Loudspeaker
  S2 = Pushbutton [package="[SMD]"]
  S1 = Pushbutton [package="[SMD]"]
  S3 = Pushbutton [package="[SMD]"]
  R2 = Resistor [tolerance=±1% resistance=220 package="0805 [SMD]"]
  R1 = Resistor [tolerance=±10% resistance=220 package="0805 [SMD]"]
  R3 = Resistor [tolerance=±10% resistance=220 package="0805 [SMD]"]
  LED2 = LED - 5mm [color="Orange (605nm)" package="5 mm [THT]"]
  LED3 = LED - 5mm [color="Red (633nm)" package="5 mm [THT]"]
  R4 = Resistor [tolerance=±10% resistance=10k package="0805 [SMD]"]
  R5 = Resistor [tolerance=±10% resistance=10k package="0805 [SMD]"]
  R6 = Resistor [tolerance=±10% resistance=10k package="0805 [SMD]"]
  part = LED - 5mm [color="Red (633nm)" package="5 mm [THT]"]  # not connected
  Part1 = Arduino Uno (Rev3)

nets:
  N1: LED1.cathode, SPKR1.pin1, LED2.cathode, LED3.cathode, R4.Pin_1, R5.Pin_1, R6.Pin_1, Part1.GND
  N2: LED1.anode, R1.Pin_1
  N3: SPKR1.pin2, Part1.D3_PWM
  N4: S2.Pin_1, S2.Pin_2, S1.Pin_1, S1.Pin_2, S3.Pin_1, S3.Pin_2, Part1.5V
  N5: S2.Pin_3, S2.Pin_4, R5.Pin_0, Part1.D11_PWM/MOSI
  N6: S1.Pin_3, S1.Pin_4, R4.Pin_0, Part1.D10_PWM/SS
  N7: S3.Pin_3, S3.Pin_4, R6.Pin_0, Part1.D12/MISO
  N8: R2.Pin_0, Part1.D7
  N9: R2.Pin_1, LED2.anode
  N10: R1.Pin_0, Part1.D6_PWM
  N11: R3.Pin_0, Part1.D8
  N12: R3.Pin_1, LED3.anode
